# Fritzing sketch TFG_Prototype_sensor (saved by Fritzing 1.0.1rc)
breadboards: 1

parts:
  RFM95W1 = RFM95W LoRa Module
  HC-SR04_Sensor_1 = HC-SR04 Ultrasonic Distance Sensor
  DHT1 = Humidity and Temperature Sensor DHT11
  MH-ET_LIVE_ESP32_DEVKIT1 = MH-ET LIVE ESP32 DEVKIT 38 pins
  Componente2 = Triple Axis Accelerometer Breakout - ADXL335
  Componente3 = Adafruit Ultimate GPS v3 [part_number="Adafruit #746"]

nets:
  GND: RFM95W1.1_GND, RFM95W1.2_MISO, RFM95W1.8_GND, RFM95W1.10_GND, RFM95W1.11_DIO3, HC-SR04_Sensor_1.GND, DHT1.GND_1, MH-ET_LIVE_ESP32_DEVKIT1.GND, MH-ET_LIVE_ESP32_DEVKIT1.IO19, Componente2.GND, Componente3.GND
  N1: RFM95W1.3_MOSI, MH-ET_LIVE_ESP32_DEVKIT1.IO23
  N2: RFM95W1.4_SCK, MH-ET_LIVE_ESP32_DEVKIT1.IO18
  N3: RFM95W1.5_NSS_(CS), MH-ET_LIVE_ESP32_DEVKIT1.IO5
  N4: RFM95W1.6_RESET, MH-ET_LIVE_ESP32_DEVKIT1.IO14
  VCC: RFM95W1.13_3.3V, HC-SR04_Sensor_1.VCC, DHT1.Vcc, MH-ET_LIVE_ESP32_DEVKIT1.3V3, Componente2.VCC, Componente3.VIN
  N5: RFM95W1.15_DIO1, MH-ET_LIVE_ESP32_DEVKIT1.IO2
  N6: HC-SR04_Sensor_1.TRIG, MH-ET_LIVE_ESP32_DEVKIT1.IO12
  N7: HC-SR04_Sensor_1.ECHO, MH-ET_LIVE_ESP32_DEVKIT1.IO13
  N8: DHT1.Data-signal, MH-ET_LIVE_ESP32_DEVKIT1.IO17
  N9: MH-ET_LIVE_ESP32_DEVKIT1.SVP, Componente2.XOUT
  N10: MH-ET_LIVE_ESP32_DEVKIT1.SVN, Componente2.YOUT
  N11: MH-ET_LIVE_ESP32_DEVKIT1.IO34, Componente2.ZOUT
  N12: MH-ET_LIVE_ESP32_DEVKIT1.TXD0, Componente3.TX
  N13: MH-ET_LIVE_ESP32_DEVKIT1.RXD0, Componente3.RX

custom parts:
  RFM95W LoRa Module: RF Transceiver by Hope RF. Well supported Arduino libraries are available. This Low Power Long Range Transceiver Module for the frequencies 868MHz and 915MHz and it is also available in other versions.
  Humidity and Temperature Sensor DHT11: Digital relative humidity & temperature sensor DHT11
  MH-ET LIVE ESP32 DEVKIT 38 pins: http://mh.nodebb.com/topic/2/mh-et-live-esp32-devkit
  Adafruit Ultimate GPS v3: We carry a few different GPS modules here in the Adafruit shop, but none that satisfied our every desire - that's why we designed this little GPS breakout board. We believe this is the Ultimate GPS module, so we named it that. It's got everything you want and more: -165 dBm sensitivity, 10 Hz updates, 66 channels 5V friendly design and only 20mA current draw Breadboard friendly + two mounting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
