# Fritzing sketch TFG_Prototype_sensor_refactor (saved by Fritzing 1.0.1rc)
breadboards: 4

parts:
  MH-ET_LIVE_ESP32_DEVKIT2 = MH-ET LIVE ESP32 DEVKIT 38 pins
  RFM95W2 = RFM95W LoRa Module
  HC-SR04_Sensor_2 = HC-SR04 Ultrasonic Distance Sensor
  DHT2 = Humidity and Temperature Sensor DHT11
  Componente4 = Triple Axis Accelerometer Breakout - ADXL335
  Componente5 = Adafruit Ultimate GPS v3 [part_number="Adafruit #746"]
  Mod1 = Heltec WiFi LoRa 32 V2 [part_number=HTIT-WB32LA]

nets:
  VCC: MH-ET_LIVE_ESP32_DEVKIT2.3V3, RFM95W2.13_3.3V, HC-SR04_Sensor_2.VCC, DHT2.Vcc, Componente4.VCC, Componente5.VIN
  N1: MH-ET_LIVE_ESP32_DEVKIT2.SVP, Componente4.XOUT
  N2: MH-ET_LIVE_ESP32_DEVKIT2.SVN, Componente4.YOUT
  N3: MH-ET_LIVE_ESP32_DEVKIT2.IO34, Componente4.ZOUT
  N4: MH-ET_LIVE_ESP32_DEVKIT2.IO25, DHT2.Data-signal
  N5: MH-ET_LIVE_ESP32_DEVKIT2.IO14, RFM95W2.6_RESET
  N6: MH-ET_LIVE_ESP32_DEVKIT2.IO12, HC-SR04_Sensor_2.TRIG
  GND: MH-ET_LIVE_ESP32_DEVKIT2.GND#58, HC-SR04_Sensor_2.GND, DHT2.GND_1, Componente4.GND
  N7: MH-ET_LIVE_ESP32_DEVKIT2.IO13, HC-SR04_Sensor_2.ECHO
  N8: MH-ET_LIVE_ESP32_DEVKIT2.GND#64, RFM95W2.1_GND, RFM95W2.10_GND, Componente5.GND
  N9: MH-ET_LIVE_ESP32_DEVKIT2.IO23, RFM95W2.3_MOSI
  N10: MH-ET_LIVE_ESP32_DEVKIT2.TXD0, Componente5.TX
  N11: MH-ET_LIVE_ESP32_DEVKIT2.RXD0, Componente5.RX
  N12: MH-ET_LIVE_ESP32_DEVKIT2.IO19, RFM95W2.2_MISO
  N13: MH-ET_LIVE_ESP32_DEVKIT2.IO18, RFM95W2.4_SCK
  N14: MH-ET_LIVE_ESP32_DEVKIT2.IO5, RFM95W2.5_NSS_(CS)
  N15: MH-ET_LIVE_ESP32_DEVKIT2.IO2, RFM95W2.15_DIO1
  N16: Mod1.pin_16, Mod1.pin_17
  N17: Mod1.pin_21, Mod1.pin_22

custom parts:
  MH-ET LIVE ESP32 DEVKIT 38 pins: http://mh.nodebb.com/topic/2/mh-et-live-esp32-devkit
  RFM95W LoRa Module: RF Transceiver by Hope RF. Well supported Arduino libraries are available. This Low Power Long Range Transceiver Module for the frequencies 868MHz and 915MHz and it is also available in other versions.
  Humidity and Temperature Sensor DHT11: Digital relative humidity & temperature sensor DHT11
  Adafruit Ultimate GPS v3: We carry a few different GPS modules here in the Adafruit shop, but none that satisfied our every desire - that's why we designed this little GPS breakout board. We believe this is the Ultimate GPS module, so we named it that. It's got everything you want and more: -165 dBm sensitivity, 10 Hz updates, 66 channels 5V friendly design and only 20mA current draw Breadboard friendly + two mounting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
